# Fritzing sketch WelFillLevelMeasuringDevice (saved by Fritzing 0.9.4)

parts:
  Bauteil1 = Arduino Ethernet Shield (Rev3)
  HC-SR04_Sensor_1 = HC-SR04 Ultrasonic Distance Sensor

nets:
  N1: Bauteil1.PWM_D5, HC-SR04_Sensor_1.TRIG
  N2: Bauteil1.PWM_D6, HC-SR04_Sensor_1.ECHO
  5V: Bauteil1.5V, HC-SR04_Sensor_1.VCC
  GND: Bauteil1.GND, HC-SR04_Sensor_1.GND
